# Fritzing sketch Autorouted (saved by Fritzing 0.9.4)

parts:
  part = Adafruit PDM Mic [part_number="Adafruit #3492"]
  RPI_Pico = Raspberry Pi Pico
  SSD_Battery_Holder = Adafruit 20mm Coin Cell Breakout Board [part_number="Adafruit #1870"]
  S1 = Toggle Switch [package=THT]
  SSD1306 = OLED Monochrome 128x64 1.3 inch [part_number=938]

nets:
  VDD: part.VDD, RPI_Pico.pin_36, S1.COM, SSD1306.3.3V
  GND: part.GND, part.SELECT, RPI_Pico.pin_8, RPI_Pico.pin_18, RPI_Pico.pin_23, RPI_Pico.pin_28, RPI_Pico.pin_38, RPI_Pico.pin_42, SSD_Battery_Holder.GND, SSD1306.GND
  N1: part.CLK, RPI_Pico.pin_5
  N2: part.DATA, RPI_Pico.pin_4
  N3: RPI_Pico.pin_21, SSD1306.MOSI_SDA
  N4: RPI_Pico.pin_22, SSD1306.SCLK_SCK
  N5: SSD_Battery_Holder.V+, S1.L1

custom parts:
  Adafruit PDM Mic: An exotic new microphone has arrived in the Adafruit shop, a PDM MEMS Microphone! PDM is the 'third' kind of microphone you can integrate with electronics, apart from analog or I2S. These microphones are very commonly used in products, but are rarely seen in maker projects. Still, they have some benefits so we thought we'd offer a breakout for the shop. The first thing to note is that this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
  Raspberry Pi Pico: Raspberry Pi Pico. Based around the RP2040 microcontroller the Pico is a low cost microcontroller device bringing Raspberry Pi quality, cost, and easy of use to the microcontroller space. Jan 2021, Split part in to two versions: SMD (this one) and tht. This one is single sided and uses the castellation pads to solder the module to the board (no holes, other than for the USB connector!). The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
  Adafruit 20mm Coin Cell Breakout Board: Simple but effective - this sewable breakout board has a CR2032 coin cell battery holder soldered on and 0.1" pitch breakout pins for easy connecting. Great for powering very low-current projects, or adding a battery backup circuit to a real-time-clock or similar.
  OLED Monochrome 128x64 1.3 inch: These displays are small, only about 1.3" diagonal, but very readable due to the high contrast of an OLED display. This display is made of 128x64 individual white OLED pixels, each one is turned on or off by the controller chip. Because the display makes its own light, no backlight is required. This reduces the power required to run the OLED and is why the display has such high contrast; we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
